# Fritzing sketch board (saved by Fritzing 0.9.2b)
breadboards: 1

parts:
  Part1 = Arduino Uno (Rev3)
  LCD1 = LCD screen
  R1 = Resistor [tolerance=±5% resistance=220 package=THT]
  R2 = Resistor [tolerance=±5% resistance=2.2k package=THT]
  DHT1 = DHT22 Humidity and Temperature Sensor
  KY-1 = Keyes Relay [package=THT]
  J1 = Screw terminal - 2 pins [package=THT]

nets:
  N1: Part1.D10_PWM/SS, KY-1.signal
  N2: Part1.D11_PWM/MOSI, LCD1.E
  N3: Part1.D12/MISO, LCD1.RS
  GND: Part1.GND, LCD1.VSS, LCD1.R/W, LCD1.LED-, R2.Pin_0, DHT1.GND, KY-1.ground
  N4: Part1.D2, LCD1.DB7
  N5: Part1.D3_PWM, LCD1.DB6
  N6: Part1.D4, LCD1.DB5
  N7: Part1.D5_PWM, LCD1.DB4
  N8: Part1.D6_PWM, DHT1.DATA
  VDD: Part1.5V, LCD1.VDD, R1.Pin_0, DHT1.VDD, KY-1.power
  N9: LCD1.V0, R2.Pin_1
  N10: LCD1.LED+, R1.Pin_1
  N11: KY-1.C, J1.pin1
  N12: KY-1.NO, J1.pin2

notes:
  To Heater

custom parts:
  Keyes Relay: The Keyes 5V relay module is suitable for SCM development, home appliance control. It uses a 5V~12V TIL control signal which can control DC / AC signal.
