# Fritzing sketch pro mini (saved by Fritzing 0.9.2b)
breadboards: 2

parts:
  Part1 = Arduino Pro Mini v13
  LCD1 = LCD screen
  RHT1 = Humidity and Temperature Sensor RHT03
  Q1 = NPN-Transistor [part_number=2n3904 package="TO92 [THT]"]
  D1 = Rectifier Diode [part_number=1N4001 package="300 mil [THT]"]
  R3 = Resistor [tolerance=±5% resistance=1k package=THT]
  VCC1 = 4 x AAA Battery Mount  # not connected
  J2 = Screw terminal - 2 pins [package=THT]
  S1 = Pushbutton [package="[THT]"]
  S2 = Pushbutton [package="[THT]"]
  S3 = Pushbutton [package="[THT]"]
  S4 = Pushbutton [package="[THT]"]
  NRF24L1 = NRF24L01
  IC1 = DS1307 [package=THT]
  XTAL1 = CRYSTAL - kHz [frequency="32 kHz"]
  Part2 = Adafruit I2C+SPI LCD Backpack [part_number="Adafruit #292"]
  R4 = Relay 5v DPDT [part_number=hk19f]
  C1 = Ceramic Capacitor [capacitance=100nF part_number=104 package="100 mil [THT, multilayer]"]

nets:
  N1: Part1.A4, Part1.A2, IC1.SDA_-_I2C_Data, Part2.DATA
  N2: Part1.A5, Part1.A3, IC1.SCL_-_I2C_Clock, Part2.CLOCK
  GND: Part1.GND, LCD1.VSS, LCD1.R/W, RHT1.GND_2, Q1.E, S1.Pin_3, S1.Pin_4, S2.Pin_3, S2.Pin_4, S3.Pin_3, S3.Pin_4, S4.Pin_3, S4.Pin_4, NRF24L1.GND, IC1.0V, Part2.GND, C1.1
  VCC: Part1.VCC, LCD1.VDD, LCD1.LED+, RHT1.Vcc, D1.cathode, IC1.+V, Part2.VCC, R4.12, C1.0
  N3: Part1.D13/SCK, NRF24L1.SCK
  N4: Part1.D12/MISO, NRF24L1.MISO
  N5: Part1.D11_PWM/MOSI, NRF24L1.MOSI
  N6: Part1.D9_PWM, R3.Pin_1
  N7: Part1.D8, NRF24L1.CSN
  N8: Part1.D7, NRF24L1.CE
  N9: Part1.D6_PWM, RHT1.Data-signal
  N10: Part1.D5_PWM, S4.Pin_1, S4.Pin_2
  N11: Part1.D4, S3.Pin_1, S3.Pin_2
  N12: Part1.D3_PWM, S2.Pin_1, S2.Pin_2
  N13: Part1.D2, S1.Pin_1, S1.Pin_2
  N14: LCD1.V0, Part2.CONTRAST
  N15: LCD1.RS, Part2.RS
  N16: LCD1.E, Part2.E
  N17: LCD1.DB0, Part2.DB0
  N18: LCD1.DB1, Part2.DB1
  N19: LCD1.DB2, Part2.DB2
  N20: LCD1.DB3, Part2.DB3
  N21: LCD1.DB4, Part2.DB4
  N22: LCD1.DB5, Part2.DB5
  N23: LCD1.DB6, Part2.DB6
  N24: LCD1.DB7, Part2.DB7
  N25: LCD1.LED-, Part2.LEDK
  N26: Q1.B, R3.Pin_0
  N27: Q1.C, D1.anode, R4.1
  N28: J2.pin1, R4.5
  N29: J2.pin2, R4.4
  N30: IC1.X1_-_Crystal, XTAL1.pin_1
  N31: IC1.X2_-_Crystal, XTAL1.pin_0

custom parts:
  NRF24L01: NRF24L01 module
  Adafruit I2C+SPI LCD Backpack: LCD backpacks reduce the number of pins needed to connect to an LCD. LCDs are a fun and easy way to have your microcontroller project talk back to you. Character LCDs are common, and easy to get, available in tons of colors and sizes. We've written tutorials on using character LCDs with an Arduino (or similar microcontroller) but find that the number of pins necessary to control the LCD can be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
  Relay 5v DPDT: 5v DPDT Relay, 8 pin

// code stored in the sketch: Untitled2.ino
// The 0.1uf capacitor connects DHT22 Vcc and Vss used to filter power supply noise, it is said in DHT22 datasheet can omit.
